// Logisim project Logisim ddca project-2.circ as structural Verilog: 1 circuit, main circuit main
module main (
  input  D,
  input  W,
  input  M,
  input  S,
  output out_5
);

  wire OR_out;

  or OR (OR_out, D, W, M);
  and AND (out_5, OR_out, S);
endmodule
